// Logisim project MIPS_Multiciclo.circ as structural Verilog: 15 circuits, main circuit main
module main (
  input  RESET,
  input  PCWriteCond,
  input  PCWrite,
  input  IorD,
  input  MemRead,
  input  MemWrite,
  input  MemToReg,
  input  IRWrite,
  input  RegDst,
  input  RegWrite,
  input  ALUsrcA,
  input  [1:0] ALUsrcB,
  input  [1:0] ALUop,
  input  [1:0] PCSource,
  input  Halfword,
  input  Manual,
  output [31:0] MLO,
  output [31:0] MHI,
  output PCWriteCond_2,
  output PCWrite_2,
  output IorD_2,
  output MemRead_2,
  output MemWrite_2,
  output MemtoReg_2,
  output IRWrite_2,
  output RegDst_2,
  output RegWrite_2,
  output ALUSrcA_2,
  output [1:0] ALUSrcB_2,
  output [1:0] ALUop_2,
  output [1:0] PCSource_2,
  output Halfword_2
);

  wire alu_1_zero, and_1_out, and_2_out, bltz_control_1_out_5, Clock, jalr_control_1_jumpreg,
       multiplexer_8_out, or_1_out;
  wire [2:0] alu_control_1_out_3, register_3_q;
  wire [4:0] instruction_register_1__15_11, instruction_register_1__25_21, multiplexer_2_out;
  wire [5:0] instruction_register_1__15_0, instruction_register_1__31_26;
  wire [15:6] instruction_register_1__15_0_2;
  wire [20:16] instruction_register_1__20_16;
  wire [27:0] shl_26_28_1_out_2;
  wire [31:0] A_q, adder_1_out, alu_1_hi, alu_1_lo, alu_1_out_5, ALU_Out_q, B_q, LH_Mux_data_o, MDR_q,
       merge_pc_1_out_3, multiplexer_1_out, multiplexer_3_out, multiplexer_4_out, multiplexer_5_out,
       multiplexer_6_out, multiplexer_7_out, PC_1_q, PC_2_q, PC_q, ram_1_data, register_1_q, register_2_q,
       register_bank_1_read_data_1, register_bank_1_read_data_2, shl_32_1_out_2, sig_ext_1_out_2;

  Clock clock_1 (.out(Clock));
  Register #(.width(32)) PC_1 (.D(PC_q), .en(Clock), .Q(PC_1_q), .clk(Clock), .clr(RESET));
  Register #(.width(32)) PC (.D(multiplexer_7_out), .en(or_1_out), .Q(PC_q), .clk(Clock), .clr(RESET));
  Register #(.width(32)) PC_2 (.D(PC_1_q), .en(Clock), .Q(PC_2_q), .clk(Clock), .clr(RESET));
  Multiplexer #(.width(32), .enable("false")) multiplexer_1 (
    .in0(PC_q), .in1(ALU_Out_q), .out(multiplexer_1_out), .sel(IorD_2));
  or or_1 (or_1_out, PCWrite_2, jalr_control_1_jumpreg, and_2_out);
  Adder #(.width(32)) adder_1 (.a(32'h4), .b(PC_2_q), .out(adder_1_out));  // open: cin, cout
  and and_1 (and_1_out, multiplexer_1_out[1], IorD_2);
  and and_2 (and_2_out, PCWriteCond_2, bltz_control_1_out_5);
  JALR_Control jalr_control_1 (
    .OPCODE(instruction_register_1__15_0), .FUNCT(instruction_register_1__31_26),
    .JumpReg(jalr_control_1_jumpreg));
  // Probe on instruction_register_1__31_26
  FSM_ROM fsm_rom_1 (
    .OPCode(instruction_register_1__31_26), .Clock(Clock), .Reset(RESET), .PCWriteCond(PCWriteCond),
    .PCWrite(PCWrite), .IorD(IorD), .MemRead(MemRead), .MemWrite(MemWrite), .MemToReg(MemToReg),
    .IRWrite(IRWrite), .RegDst(RegDst), .RegWrite(RegWrite), .ALUsrcA(ALUsrcA), .ALUsrcB(ALUsrcB),
    .ALUop(ALUop), .PCSource(PCSource), .Halfword(Halfword), .Debug(Manual), .PCWriteCond_2(PCWriteCond_2),
    .PCWrite_2(PCWrite_2), .IorD_2(IorD_2), .MemRead_2(MemRead_2), .MemWrite_2(MemWrite_2),
    .MemtoReg_2(MemtoReg_2), .IRWrite_2(IRWrite_2), .RegDst_2(RegDst_2), .RegWrite_2(RegWrite_2),
    .ALUSrcA_2(ALUSrcA_2), .ALUSrcB_2(ALUSrcB_2), .ALUop_2(ALUop_2), .PCSource_2(PCSource_2),
    .Halfword_2(Halfword_2));
  RAM #(.addrWidth(24), .dataWidth(32), .bus("separate")) ram_1 (
    .addr(multiplexer_1_out[25:2]), .din(B_q), .data(ram_1_data), .str(MemWrite_2), .sel(1'b1), .clk(Clock),
    .ld(MemRead_2), .clr(1'b0));
  lh_mux LH_Mux (.Data_i(ram_1_data), .Upper(and_1_out), .Halfword(Halfword_2), .Data_o(LH_Mux_data_o));
  Instruction_Register instruction_register_1 (
    .in_1(ram_1_data), .Enable(IRWrite_2), .Reset(RESET), .Clock(Clock),
    ._31_26(instruction_register_1__31_26), ._25_21(instruction_register_1__25_21),
    ._20_16(instruction_register_1__20_16), ._15_11(instruction_register_1__15_11),
    ._15_0({instruction_register_1__15_0_2, instruction_register_1__15_0}));
  Register #(.width(32)) MDR (.D(LH_Mux_data_o), .en(1'b1), .Q(MDR_q), .clk(Clock), .clr(RESET));
  // Probe on instruction_register_1__31_26
  Multiplexer #(.width(5), .enable("false")) multiplexer_2 (
    .in0(instruction_register_1__20_16), .in1(instruction_register_1__15_11), .out(multiplexer_2_out),
    .sel(RegDst_2));
  Multiplexer #(.width(32), .enable("false")) multiplexer_3 (
    .in0(ALU_Out_q), .in1(MDR_q), .out(multiplexer_3_out), .sel(MemtoReg_2));
  Multiplexer #(.width(32), .enable("false")) multiplexer_4 (
    .in0(multiplexer_3_out), .in1(adder_1_out), .out(multiplexer_4_out), .sel(jalr_control_1_jumpreg));
  Register_Bank register_bank_1 (
    .Read_1_Address(instruction_register_1__25_21), .Read_2_Address(instruction_register_1__20_16),
    .Write_Address(multiplexer_2_out), .Write_Data(multiplexer_4_out), .Enable(RegWrite_2), .Reset(RESET),
    .Clock(Clock), .Read_Data_1(register_bank_1_read_data_1), .Read_Data_2(register_bank_1_read_data_2));
  sig_ext sig_ext_1 (.in_1({instruction_register_1__15_0_2, instruction_register_1__15_0}), .out_2(sig_ext_1_out_2));
  shl_26_28 shl_26_28_1 (
    .in_1({instruction_register_1__25_21, instruction_register_1__20_16, instruction_register_1__15_0_2, instruction_register_1__15_0}),
    .out_2(shl_26_28_1_out_2));
  Register #(.width(32)) A (.D(register_bank_1_read_data_1), .en(1'b1), .Q(A_q), .clk(Clock), .clr(RESET));
  Register #(.width(32)) B (.D(register_bank_1_read_data_2), .en(1'b1), .Q(B_q), .clk(Clock), .clr(RESET));
  shl_32 shl_32_1 (.in_1(sig_ext_1_out_2), .out_2(shl_32_1_out_2));
  merge_PC merge_pc_1 (.in_1(shl_26_28_1_out_2), .in_2(PC_q[31:28]), .out_3(merge_pc_1_out_3));
  Multiplexer #(.width(32), .enable("false")) multiplexer_5 (
    .in0(PC_q), .in1(A_q), .out(multiplexer_5_out), .sel(ALUSrcA_2));
  Multiplexer #(.select(2), .width(32), .enable("false")) multiplexer_6 (
    .in0(B_q), .in1(32'h4), .in2(sig_ext_1_out_2), .in3(shl_32_1_out_2), .out(multiplexer_6_out),
    .sel(ALUSrcB_2));
  ALU alu_1 (
    .in_1(multiplexer_5_out), .in_2(multiplexer_6_out), .in_3(alu_control_1_out_3), .Zero(alu_1_zero),
    .out_5(alu_1_out_5), .LO(alu_1_lo), .HI(alu_1_hi));
  Register #(.width(32)) ALU_Out (.D(alu_1_out_5), .en(1'b1), .Q(ALU_Out_q), .clk(Clock), .clr(RESET));
  ALU_Control alu_control_1 (.in_1(ALUop_2), .in_2(instruction_register_1__15_0), .out_3(alu_control_1_out_3));
  BLTZ_Control bltz_control_1 (
    .rs(A_q), .bltz(instruction_register_1__20_16), .in_3(alu_1_zero), .op(instruction_register_1__31_26),
    .out_5(bltz_control_1_out_5));
  Multiplexer #(.select(2), .width(32), .enable("false")) multiplexer_7 (
    .in0(alu_1_out_5), .in1(ALU_Out_q), .in2(merge_pc_1_out_3), .out(multiplexer_7_out), .sel(PCSource_2));  // open: in3
  // Probe on multiplexer_7_out
  Register #(.width(32)) register_1 (.D(alu_1_lo), .en(1'b1), .Q(register_1_q), .clk(Clock), .clr(RESET));
  Register #(.width(32)) register_2 (.D(alu_1_hi), .en(1'b1), .Q(register_2_q), .clk(Clock), .clr(RESET));
  Register #(.width(3)) register_3 (.D(alu_control_1_out_3), .en(1'b1), .Q(register_3_q), .clk(Clock), .clr(RESET));
  Multiplexer #(.select(3), .disabled(0), .enable("false")) multiplexer_8 (
    .in0(1'b0), .in1(1'b0), .in2(1'b0), .in3(RegWrite_2), .in4(1'b0), .in5(1'b0), .in6(1'b0), .in7(1'b0),
    .out(multiplexer_8_out), .sel(register_3_q));
  Register #(.width(32)) reg_mlo (.D(register_1_q), .en(multiplexer_8_out), .Q(MLO), .clk(Clock), .clr(RESET));
  Register #(.width(32)) reg_mhi (.D(register_2_q), .en(multiplexer_8_out), .Q(MHI), .clk(Clock), .clr(RESET));

  // Notes on the sheet:
  //   Bloco Operativo
  //   Bloco de Controle
  //   Memory
  //   Upper
  //   IR
  //   inst 25-0
  //   inst 15-11
  //   Sig ext
  //   Reg. Bank
  //   shl
  //   conc PC 31_28
  //   shl_26_28
  //   bltz
  //   ALU
  //   ALU Control
endmodule

module Instruction_Register (
  input  [31:0] in_1,
  input  Enable,
  input  Reset,
  input  Clock,
  output [5:0] _31_26,
  output [4:0] _25_21,
  output [4:0] _20_16,
  output [4:0] _15_11,
  output [15:0] _15_0
);

  Register #(.width(32)) register_1 (
    .D(in_1), .en(Enable), .Q({_31_26, _25_21, _20_16, _15_0}), .clk(Clock), .clr(Reset));

  assign _15_11 = _15_0[15:11];
endmodule

module Register_Bank (
  input  [4:0] Read_1_Address,
  input  [4:0] Read_2_Address,
  input  [4:0] Write_Address,
  input  [31:0] Write_Data,
  input  Enable,
  input  Reset,
  input  Clock,
  output [31:0] Read_Data_1,
  output [31:0] Read_Data_2
);

  wire and_1_out, and_2_out, and_3_out, and_4_out, and_5_out, and_6_out, and_7_out, and_8_out, and_9_out,
       and_10_out, and_11_out, and_12_out, and_13_out, and_14_out, and_15_out, and_16_out, and_17_out,
       and_18_out, and_19_out, and_20_out, and_21_out, and_22_out, and_23_out, and_24_out, and_25_out,
       and_26_out, and_27_out, and_28_out, and_29_out, and_30_out, and_31_out, and_32_out, dec_5_1_1_out_2,
       dec_5_1_1_out_3, dec_5_1_1_out_4, dec_5_1_1_out_5, dec_5_1_1_out_6, dec_5_1_1_out_7, dec_5_1_1_out_8,
       dec_5_1_1_out_9, dec_5_1_1_out_10, dec_5_1_1_out_11, dec_5_1_1_out_12, dec_5_1_1_out_13,
       dec_5_1_1_out_14, dec_5_1_1_out_15, dec_5_1_1_out_16, dec_5_1_1_out_17, dec_5_1_1_out_18,
       dec_5_1_1_out_19, dec_5_1_1_out_20, dec_5_1_1_out_21, dec_5_1_1_out_22, dec_5_1_1_out_23,
       dec_5_1_1_out_24, dec_5_1_1_out_25, dec_5_1_1_out_26, dec_5_1_1_out_27, dec_5_1_1_out_28,
       dec_5_1_1_out_29, dec_5_1_1_out_30, dec_5_1_1_out_31, dec_5_1_1_out_32, dec_5_1_1_out_33;
  wire [31:0] multiplexer_1_out, multiplexer_2_out, multiplexer_3_out, multiplexer_4_out, register_2_q,
       register_3_q, register_4_q, register_5_q, register_6_q, register_7_q, register_8_q, register_9_q,
       register_10_q, register_11_q, register_12_q, register_13_q, register_14_q, register_15_q,
       register_16_q, register_17_q, register_18_q, register_19_q, register_20_q, register_21_q,
       register_22_q, register_23_q, register_24_q, register_25_q, register_26_q, register_27_q,
       register_28_q, register_29_q, register_30_q, register_31_q, register_32_q;

  Dec_5_1 dec_5_1_1 (
    .in_1(Write_Address), .out_2(dec_5_1_1_out_2), .out_3(dec_5_1_1_out_3), .out_4(dec_5_1_1_out_4),
    .out_5(dec_5_1_1_out_5), .out_6(dec_5_1_1_out_6), .out_7(dec_5_1_1_out_7), .out_8(dec_5_1_1_out_8),
    .out_9(dec_5_1_1_out_9), .out_10(dec_5_1_1_out_10), .out_11(dec_5_1_1_out_11), .out_12(dec_5_1_1_out_12),
    .out_13(dec_5_1_1_out_13), .out_14(dec_5_1_1_out_14), .out_15(dec_5_1_1_out_15),
    .out_16(dec_5_1_1_out_16), .out_17(dec_5_1_1_out_17), .out_18(dec_5_1_1_out_18),
    .out_19(dec_5_1_1_out_19), .out_20(dec_5_1_1_out_20), .out_21(dec_5_1_1_out_21),
    .out_22(dec_5_1_1_out_22), .out_23(dec_5_1_1_out_23), .out_24(dec_5_1_1_out_24),
    .out_25(dec_5_1_1_out_25), .out_26(dec_5_1_1_out_26), .out_27(dec_5_1_1_out_27),
    .out_28(dec_5_1_1_out_28), .out_29(dec_5_1_1_out_29), .out_30(dec_5_1_1_out_30),
    .out_31(dec_5_1_1_out_31), .out_32(dec_5_1_1_out_32), .out_33(dec_5_1_1_out_33));
  and and_1 (and_1_out, dec_5_1_1_out_2, Enable);
  and and_2 (and_2_out, dec_5_1_1_out_3, Enable);
  and and_3 (and_3_out, dec_5_1_1_out_4, Enable);
  and and_4 (and_4_out, dec_5_1_1_out_5, Enable);
  and and_5 (and_5_out, dec_5_1_1_out_6, Enable);
  and and_6 (and_6_out, dec_5_1_1_out_7, Enable);
  and and_7 (and_7_out, dec_5_1_1_out_8, Enable);
  and and_8 (and_8_out, dec_5_1_1_out_9, Enable);
  and and_9 (and_9_out, dec_5_1_1_out_10, Enable);
  and and_10 (and_10_out, dec_5_1_1_out_11, Enable);
  and and_11 (and_11_out, dec_5_1_1_out_12, Enable);
  and and_12 (and_12_out, dec_5_1_1_out_13, Enable);
  and and_13 (and_13_out, dec_5_1_1_out_14, Enable);
  and and_14 (and_14_out, dec_5_1_1_out_15, Enable);
  and and_15 (and_15_out, dec_5_1_1_out_16, Enable);
  and and_16 (and_16_out, dec_5_1_1_out_17, Enable);
  and and_17 (and_17_out, dec_5_1_1_out_18, Enable);
  and and_18 (and_18_out, dec_5_1_1_out_19, Enable);
  and and_19 (and_19_out, dec_5_1_1_out_20, Enable);
  and and_20 (and_20_out, dec_5_1_1_out_21, Enable);
  and and_21 (and_21_out, dec_5_1_1_out_22, Enable);
  and and_22 (and_22_out, dec_5_1_1_out_23, Enable);
  and and_23 (and_23_out, dec_5_1_1_out_24, Enable);
  and and_24 (and_24_out, dec_5_1_1_out_25, Enable);
  and and_25 (and_25_out, dec_5_1_1_out_26, Enable);
  and and_26 (and_26_out, dec_5_1_1_out_27, Enable);
  and and_27 (and_27_out, dec_5_1_1_out_28, Enable);
  and and_28 (and_28_out, dec_5_1_1_out_29, Enable);
  and and_29 (and_29_out, dec_5_1_1_out_30, Enable);
  and and_30 (and_30_out, dec_5_1_1_out_31, Enable);
  and and_31 (and_31_out, dec_5_1_1_out_32, Enable);
  and and_32 (and_32_out, dec_5_1_1_out_33, Enable);
  Register #(.width(32)) register_1 (.D(Write_Data), .en(and_1_out), .clk(Clock), .clr(Reset));  // open: Q
  Register #(.width(32)) register_2 (.D(Write_Data), .en(and_2_out), .Q(register_2_q), .clk(Clock), .clr(Reset));
  Register #(.width(32)) register_3 (.D(Write_Data), .en(and_3_out), .Q(register_3_q), .clk(Clock), .clr(Reset));
  Register #(.width(32)) register_4 (.D(Write_Data), .en(and_4_out), .Q(register_4_q), .clk(Clock), .clr(Reset));
  Register #(.width(32)) register_5 (.D(Write_Data), .en(and_5_out), .Q(register_5_q), .clk(Clock), .clr(Reset));
  Register #(.width(32)) register_6 (.D(Write_Data), .en(and_6_out), .Q(register_6_q), .clk(Clock), .clr(Reset));
  Register #(.width(32)) register_7 (.D(Write_Data), .en(and_7_out), .Q(register_7_q), .clk(Clock), .clr(Reset));
  Register #(.width(32)) register_8 (.D(Write_Data), .en(and_8_out), .Q(register_8_q), .clk(Clock), .clr(Reset));
  Register #(.width(32)) register_9 (.D(Write_Data), .en(and_9_out), .Q(register_9_q), .clk(Clock), .clr(Reset));
  Register #(.width(32)) register_10 (.D(Write_Data), .en(and_10_out), .Q(register_10_q), .clk(Clock), .clr(Reset));
  Register #(.width(32)) register_11 (.D(Write_Data), .en(and_11_out), .Q(register_11_q), .clk(Clock), .clr(Reset));
  Register #(.width(32)) register_12 (.D(Write_Data), .en(and_12_out), .Q(register_12_q), .clk(Clock), .clr(Reset));
  Register #(.width(32)) register_13 (.D(Write_Data), .en(and_13_out), .Q(register_13_q), .clk(Clock), .clr(Reset));
  Register #(.width(32)) register_14 (.D(Write_Data), .en(and_14_out), .Q(register_14_q), .clk(Clock), .clr(Reset));
  Register #(.width(32)) register_15 (.D(Write_Data), .en(and_15_out), .Q(register_15_q), .clk(Clock), .clr(Reset));
  Register #(.width(32)) register_16 (.D(Write_Data), .en(and_16_out), .Q(register_16_q), .clk(Clock), .clr(Reset));
  Register #(.width(32)) register_17 (.D(Write_Data), .en(and_17_out), .Q(register_17_q), .clk(Clock), .clr(Reset));
  Register #(.width(32)) register_18 (.D(Write_Data), .en(and_18_out), .Q(register_18_q), .clk(Clock), .clr(Reset));
  Register #(.width(32)) register_19 (.D(Write_Data), .en(and_19_out), .Q(register_19_q), .clk(Clock), .clr(Reset));
  Register #(.width(32)) register_20 (.D(Write_Data), .en(and_20_out), .Q(register_20_q), .clk(Clock), .clr(Reset));
  Register #(.width(32)) register_21 (.D(Write_Data), .en(and_21_out), .Q(register_21_q), .clk(Clock), .clr(Reset));
  Register #(.width(32)) register_22 (.D(Write_Data), .en(and_22_out), .Q(register_22_q), .clk(Clock), .clr(Reset));
  Register #(.width(32)) register_23 (.D(Write_Data), .en(and_23_out), .Q(register_23_q), .clk(Clock), .clr(Reset));
  Register #(.width(32)) register_24 (.D(Write_Data), .en(and_24_out), .Q(register_24_q), .clk(Clock), .clr(Reset));
  Register #(.width(32)) register_25 (.D(Write_Data), .en(and_25_out), .Q(register_25_q), .clk(Clock), .clr(Reset));
  Register #(.width(32)) register_26 (.D(Write_Data), .en(and_26_out), .Q(register_26_q), .clk(Clock), .clr(Reset));
  Register #(.width(32)) register_27 (.D(Write_Data), .en(and_27_out), .Q(register_27_q), .clk(Clock), .clr(Reset));
  Register #(.width(32)) register_28 (.D(Write_Data), .en(and_28_out), .Q(register_28_q), .clk(Clock), .clr(Reset));
  Register #(.width(32)) register_29 (.D(Write_Data), .en(and_29_out), .Q(register_29_q), .clk(Clock), .clr(Reset));
  Register #(.width(32)) register_30 (.D(Write_Data), .en(and_30_out), .Q(register_30_q), .clk(Clock), .clr(Reset));
  Register #(.width(32)) register_31 (.D(Write_Data), .en(and_31_out), .Q(register_31_q), .clk(Clock), .clr(Reset));
  Register #(.width(32)) register_32 (.D(Write_Data), .en(and_32_out), .Q(register_32_q), .clk(Clock), .clr(Reset));
  Multiplexer #(.select(4), .width(32), .enable("false")) multiplexer_1 (
    .in0({32{1'b0}}), .in1(register_2_q), .in2(register_3_q), .in3(register_4_q), .in4(register_5_q),
    .in5(register_6_q), .in6(register_7_q), .in7(register_8_q), .in8(register_9_q), .in9(register_10_q),
    .in10(register_11_q), .in11(register_12_q), .in12(register_13_q), .in13(register_14_q),
    .in14(register_15_q), .in15(register_16_q), .out(multiplexer_1_out), .sel(Read_2_Address[3:0]));
  Multiplexer #(.select(4), .width(32), .enable("false")) multiplexer_2 (
    .in0({32{1'b0}}), .in1(register_2_q), .in2(register_3_q), .in3(register_4_q), .in4(register_5_q),
    .in5(register_6_q), .in6(register_7_q), .in7(register_8_q), .in8(register_9_q), .in9(register_10_q),
    .in10(register_11_q), .in11(register_12_q), .in12(register_13_q), .in13(register_14_q),
    .in14(register_15_q), .in15(register_16_q), .out(multiplexer_2_out), .sel(Read_1_Address[3:0]));
  Multiplexer #(.select(4), .width(32), .enable("false")) multiplexer_3 (
    .in0(register_17_q), .in1(register_18_q), .in2(register_19_q), .in3(register_20_q), .in4(register_21_q),
    .in5(register_22_q), .in6(register_23_q), .in7(register_24_q), .in8(register_25_q), .in9(register_26_q),
    .in10(register_27_q), .in11(register_28_q), .in12(register_29_q), .in13(register_30_q),
    .in14(register_31_q), .in15(register_32_q), .out(multiplexer_3_out), .sel(Read_1_Address[3:0]));
  Multiplexer #(.select(4), .width(32), .enable("false")) multiplexer_4 (
    .in0(register_17_q), .in1(register_18_q), .in2(register_19_q), .in3(register_20_q), .in4(register_21_q),
    .in5(register_22_q), .in6(register_23_q), .in7(register_24_q), .in8(register_25_q), .in9(register_26_q),
    .in10(register_27_q), .in11(register_28_q), .in12(register_29_q), .in13(register_30_q),
    .in14(register_31_q), .in15(register_32_q), .out(multiplexer_4_out), .sel(Read_2_Address[3:0]));
  Multiplexer #(.width(32), .enable("false")) multiplexer_5 (
    .in0(multiplexer_2_out), .in1(multiplexer_3_out), .out(Read_Data_1), .sel(Read_1_Address[4]));
  Multiplexer #(.width(32), .enable("false")) multiplexer_6 (
    .in0(multiplexer_1_out), .in1(multiplexer_4_out), .out(Read_Data_2), .sel(Read_2_Address[4]));
endmodule

module Dec_5_1 (
  input  [4:0] in_1,
  output out_2,
  output out_3,
  output out_4,
  output out_5,
  output out_6,
  output out_7,
  output out_8,
  output out_9,
  output out_10,
  output out_11,
  output out_12,
  output out_13,
  output out_14,
  output out_15,
  output out_16,
  output out_17,
  output out_18,
  output out_19,
  output out_20,
  output out_21,
  output out_22,
  output out_23,
  output out_24,
  output out_25,
  output out_26,
  output out_27,
  output out_28,
  output out_29,
  output out_30,
  output out_31,
  output out_32,
  output out_33
);

  wire decoder_1_out0, decoder_2_out0, not_1_out, not_2_out, not_3_out, not_4_out;
  wire [3:0] and_1_out, and_5_out;

  not not_1 (not_1_out, in_1[4]);
  not not_2 (not_2_out, in_1[4]);
  not not_3 (not_3_out, in_1[4]);
  not not_4 (not_4_out, in_1[4]);
  and and_1 (and_1_out[0], not_1_out, in_1[0]);
  and and_2 (and_1_out[1], not_2_out, in_1[1]);
  and and_3 (and_1_out[2], not_3_out, in_1[2]);
  and and_4 (and_1_out[3], not_4_out, in_1[3]);
  and and_5 (and_5_out[0], in_1[4], in_1[0]);
  and and_6 (and_5_out[1], in_1[4], in_1[1]);
  and and_7 (and_5_out[2], in_1[4], in_1[2]);
  and and_8 (and_5_out[3], in_1[4], in_1[3]);
  Decoder #(.select(4), .enable("false")) decoder_1 (
    .out0(decoder_1_out0), .out1(out_3), .out2(out_4), .out3(out_5), .out4(out_6), .out5(out_7),
    .out6(out_8), .out7(out_9), .out8(out_10), .out9(out_11), .out10(out_12), .out11(out_13), .out12(out_14),
    .out13(out_15), .out14(out_16), .out15(out_17), .sel(and_1_out));
  Decoder #(.select(4), .enable("false")) decoder_2 (
    .out0(decoder_2_out0), .out1(out_19), .out2(out_20), .out3(out_21), .out4(out_22), .out5(out_23),
    .out6(out_24), .out7(out_25), .out8(out_26), .out9(out_27), .out10(out_28), .out11(out_29),
    .out12(out_30), .out13(out_31), .out14(out_32), .out15(out_33), .sel(and_5_out));
  and and_9 (out_2, not_1_out, decoder_1_out0);
  and and_10 (out_18, in_1[4], decoder_2_out0);
endmodule

module ALU (
  input  [31:0] in_1,
  input  [31:0] in_2,
  input  [2:0] in_3,
  output Zero,
  output [31:0] out_5,
  output [31:0] LO,
  output [31:0] HI
);

  wire or_2_out, or_3_out, or_4_out, or_5_out, or_6_out;
  wire [31:0] adder_1_out, and_1_out, or_1_out, subtractor_1_out;

  assign and_1_out = in_1 & in_2;  // AND_Gate and_1, 32 bits wide
  assign or_1_out = in_1 | in_2;  // OR_Gate or_1, 32 bits wide
  Adder #(.width(32)) adder_1 (.a(in_1), .b(in_2), .out(adder_1_out));  // open: cin, cout
  Subtractor #(.width(32)) subtractor_1 (.a(in_1), .b(in_2), .out(subtractor_1_out));  // open: bin, bout
  Multiplier #(.width(32)) multiplier_1 (.a(in_1), .b(in_2), .out(LO), .cout(HI));  // open: cin
  Multiplexer #(.select(3), .width(32), .enable("false")) multiplexer_1 (
    .in0(and_1_out), .in1(or_1_out), .in2(adder_1_out), .in3(or_1_out), .in6(subtractor_1_out),
    .in7({{31{1'b0}}, subtractor_1_out[31]}), .out(out_5), .sel(in_3));  // open: in4, in5
  or or_2 (or_2_out, out_5[0], out_5[1], out_5[2], out_5[3], out_5[4], out_5[5], out_5[6], out_5[7], out_5[8]);
  or or_3 (or_3_out, out_5[9], out_5[10], out_5[11], out_5[12], out_5[13], out_5[14], out_5[15], out_5[16], out_5[17]);
  or or_4 (or_4_out, out_5[18], out_5[19], out_5[20], out_5[21], out_5[22], out_5[23], out_5[24], out_5[25], out_5[26]);
  or or_5 (or_5_out, out_5[27], out_5[28], out_5[29], out_5[30], out_5[31]);
  or or_6 (or_6_out, or_2_out, or_3_out, or_4_out, or_5_out);
  not not_1 (Zero, or_6_out);
endmodule

module shl_26_28 (
  input  [25:0] in_1,
  output [27:0] out_2
);


  assign out_2 = {in_1, 2'b00};
endmodule

module merge_PC (
  input  [27:0] in_1,
  input  [3:0] in_2,
  output [31:0] out_3
);


  assign out_3 = {in_2, in_1};
endmodule

module sig_ext (
  input  [15:0] in_1,
  output [31:0] out_2
);


  assign out_2 = {{17{in_1[15]}}, in_1[14:0]};
endmodule

module shl_32 (
  input  [31:0] in_1,
  output [31:0] out_2
);


  assign out_2 = {in_1[29:0], 2'b00};
endmodule

module ALU_Control (
  input  [1:0] in_1,
  input  [5:0] in_2,
  output [2:0] out_3
);

  wire and_1_out, not_1_out, not_2_out, or_1_out;

  or or_1 (or_1_out, in_2[2], in_2[5]);
  and and_1 (and_1_out, in_1[1], in_2[4]);
  and and_2 (out_3[0], in_1[1], or_1_out);
  not not_1 (not_1_out, in_1[1]);
  not not_2 (not_2_out, in_2[3]);
  or or_2 (out_3[2], in_1[0], and_1_out);
  or or_3 (out_3[1], not_1_out, not_2_out);
endmodule

module Debug_Register_Bank (
  input  Debug,
  input  Debug_Enable,
  input  [4:0] Debug_Write_Address,
  input  [31:0] Debug_Write_Data,
  input  [4:0] Read_1_Address,
  input  [4:0] Read_2_Address,
  input  [4:0] Write_Address,
  input  [31:0] Write_Data,
  input  Enable,
  input  Reset,
  input  Clock,
  output [31:0] Read_Data_1,
  output [31:0] Read_Data_2
);

  wire and_1_out, not_1_out, or_1_out;
  wire [4:0] multiplexer_1_out;
  wire [31:0] multiplexer_2_out;

  not not_1 (not_1_out, Debug);
  Multiplexer #(.width(5), .enable("false")) multiplexer_1 (
    .in0(Write_Address), .in1(Debug_Write_Address), .out(multiplexer_1_out), .sel(Debug));
  Multiplexer #(.width(32), .enable("false")) multiplexer_2 (
    .in0(Write_Data), .in1(Debug_Write_Data), .out(multiplexer_2_out), .sel(Debug));
  or or_1 (or_1_out, Debug_Enable, Enable);
  and and_1 (and_1_out, not_1_out, Reset);
  Register_Bank register_bank_1 (
    .Read_1_Address(Read_1_Address), .Read_2_Address(Read_2_Address), .Write_Address(multiplexer_1_out),
    .Write_Data(multiplexer_2_out), .Enable(or_1_out), .Reset(and_1_out), .Clock(Clock),
    .Read_Data_1(Read_Data_1), .Read_Data_2(Read_Data_2));
endmodule

module FSM_ROM (
  input  [5:0] OPCode,
  input  Clock,
  input  Reset,
  input  PCWriteCond,
  input  PCWrite,
  input  IorD,
  input  MemRead,
  input  MemWrite,
  input  MemToReg,
  input  IRWrite,
  input  RegDst,
  input  RegWrite,
  input  ALUsrcA,
  input  [1:0] ALUsrcB,
  input  [1:0] ALUop,
  input  [1:0] PCSource,
  input  Halfword,
  input  Debug,
  output PCWriteCond_2,
  output PCWrite_2,
  output IorD_2,
  output MemRead_2,
  output MemWrite_2,
  output MemtoReg_2,
  output IRWrite_2,
  output RegDst_2,
  output RegWrite_2,
  output ALUSrcA_2,
  output [1:0] ALUSrcB_2,
  output [1:0] ALUop_2,
  output [1:0] PCSource_2,
  output Halfword_2
);

  wire [3:0] Current_State_q, rom_2_data;
  wire [16:0] rom_1_data;

  ROM #(.addrWidth(4), .dataWidth(17)) rom_1 (.addr(Current_State_q), .data(rom_1_data), .sel(1'b1));
  ROM #(.addrWidth(10), .dataWidth(4)) rom_2 (.addr({OPCode, Current_State_q}), .data(rom_2_data), .sel(1'b1));
  Register #(.width(4)) Current_State (.D(rom_2_data), .en(1'b1), .Q(Current_State_q), .clk(Clock), .clr(Reset));
  Multiplexer #(.enable("false")) multiplexer_1 (
    .in0(rom_1_data[15]), .in1(PCWriteCond), .out(PCWriteCond_2), .sel(Debug));
  Multiplexer #(.enable("false")) multiplexer_2 (.in0(rom_1_data[14]), .in1(PCWrite), .out(PCWrite_2), .sel(Debug));
  Multiplexer #(.enable("false")) multiplexer_3 (.in0(rom_1_data[13]), .in1(IorD), .out(IorD_2), .sel(Debug));
  Multiplexer #(.enable("false")) multiplexer_4 (.in0(rom_1_data[12]), .in1(MemRead), .out(MemRead_2), .sel(Debug));
  Multiplexer #(.enable("false")) multiplexer_5 (.in0(rom_1_data[11]), .in1(MemWrite), .out(MemWrite_2), .sel(Debug));
  Multiplexer #(.enable("false")) multiplexer_6 (.in0(rom_1_data[10]), .in1(MemToReg), .out(MemtoReg_2), .sel(Debug));
  Multiplexer #(.enable("false")) multiplexer_7 (.in0(rom_1_data[9]), .in1(IRWrite), .out(IRWrite_2), .sel(Debug));
  Multiplexer #(.enable("false")) multiplexer_8 (.in0(rom_1_data[8]), .in1(RegDst), .out(RegDst_2), .sel(Debug));
  Multiplexer #(.enable("false")) multiplexer_9 (.in0(rom_1_data[7]), .in1(RegWrite), .out(RegWrite_2), .sel(Debug));
  Multiplexer #(.enable("false")) multiplexer_10 (.in0(rom_1_data[6]), .in1(ALUsrcA), .out(ALUSrcA_2), .sel(Debug));
  Multiplexer #(.width(2), .enable("false")) multiplexer_11 (
    .in0(rom_1_data[5:4]), .in1(ALUsrcB), .out(ALUSrcB_2), .sel(Debug));
  Multiplexer #(.width(2), .enable("false")) multiplexer_12 (
    .in0(rom_1_data[3:2]), .in1(ALUop), .out(ALUop_2), .sel(Debug));
  Multiplexer #(.width(2), .enable("false")) multiplexer_13 (
    .in0(rom_1_data[1:0]), .in1(PCSource), .out(PCSource_2), .sel(Debug));
  Multiplexer #(.enable("false")) multiplexer_14 (.in0(rom_1_data[16]), .in1(Halfword), .out(Halfword_2), .sel(Debug));

  // Notes on the sheet:
  //   Geração da saída
  //   opcode + estado
  //   Próximo Estado
  //   contents of rom_1 (hex, n*v repeats v):
  //   5210 30 60 3000 480 2800 48 180 8045 4002 13000 0 0 0 80 60
  //   contents of rom_2 (hex, n*v repeats v):
  //   1 6 4*0 7 9*0 1 8 14*0 1 9 30*0 1 8 63*0 f 13*0 e 384*0 1 2 a 7*0 4 21*0 1 2 3 4 124*0 1 2 5
endmodule

module lh_mux (
  input  [31:0] Data_i,
  input  Halfword,
  input  Upper,
  output [31:0] Data_o
);

  wire [15:0] multiplexer_1_out;

  Multiplexer #(.width(16), .enable("false")) multiplexer_1 (
    .in0(Data_i[15:0]), .in1(Data_i[31:16]), .out(multiplexer_1_out), .sel(Upper));
  Multiplexer #(.width(32), .disabled(0), .enable("false")) multiplexer_2 (
    .in0(Data_i), .in1({{17{multiplexer_1_out[15]}}, multiplexer_1_out[14:0]}), .out(Data_o), .sel(Halfword));
endmodule

module JALR_Control (
  input  [5:0] OPCODE,
  input  [5:0] FUNCT,
  output JumpReg
);

  wire and_1_out, and_2_out;

  and and_1 (and_1_out, ~OPCODE[0], ~OPCODE[1], ~OPCODE[2], ~OPCODE[3], ~OPCODE[4], ~OPCODE[5]);  // AND_Gate
  and and_2 (and_2_out, FUNCT[0], ~FUNCT[1], ~FUNCT[2], FUNCT[3], ~FUNCT[4], ~FUNCT[5]);  // AND_Gate
  and and_3 (JumpReg, and_1_out, and_2_out);

  // Notes on the sheet:
  //   OPCODE = 000000 (SPECIAL)
  //   FUNCT = 001001 (JALR)
endmodule

module BLTZ_Control (
  input  [31:0] rs,
  input  [4:0] bltz,
  input  in_3,
  input  [5:0] op,
  output out_5
);

  wire and_1_out, and_2_out, nor_1_out;

  nor nor_1 (nor_1_out, bltz[0], bltz[1], bltz[2], bltz[3], bltz[4]);
  and and_1 (and_1_out, op[0], ~op[1], ~op[2], ~op[3], ~op[4], ~op[5]);  // AND_Gate
  and and_2 (and_2_out, rs[31], nor_1_out, and_1_out);
  or or_1 (out_5, and_2_out, in_3);
endmodule
